// Logisim project elephant_corridor_monitor.circ as structural Verilog: 1 circuit, main circuit main
module main (
  input  [3:0] Proximity,
  input  [1:0] Direction,
  input  [3:0] Speed,
  input  TimeOfDay,
  input  CrossingPulse,
  output LED_GREEN,
  output LED_YELLOW,
  output LED_RED,
  output BUZZER_ALARM,
  output [1:0] ZoneStatus
);
endmodule
