// Logisim project elephant_corridor_monitor_working.circ as structural Verilog: 2 circuits, main circuit main
module main (
  input  [3:0] Proximity,
  input  [1:0] Direction,
  input  [3:0] Speed,
  input  TimeOfDay,
  input  [1:0] in_5,
  input  in_6,
  input  CLK,
  input  Reset,
  output LED_GREEN,
  output LED_YELLOW,
  output LED_RED,
  output BUZZER_ALARM,
  output [1:0] ZoneDIsplay,
  output [7:0] out_14,
  output [7:0] out_15,
  output [7:0] out_16,
  output [7:0] out_17
);

  wire and_1_out, and_2_out, and_3_out, and_6_out, comparator_2_gt, comparator_3_gt, comparator_4_gt,
       comparator_5_gt, not_1_out, not_2_out, not_3_out, not_4_out, not_5_out, not_6_out, not_8_out,
       or_2_out, or_3_out;

  not not_1 (not_1_out, Direction[1]);
  not not_2 (not_2_out, Direction[0]);
  Comparator #(.mode("unsigned"), .width(4)) comparator_1 (
    .a(Proximity), .b(4'b0100), .gt(ZoneDIsplay[1]));  // open: eq, lt
  Comparator #(.mode("unsigned"), .width(4)) comparator_2 (
    .a(Proximity), .b(4'b1000), .gt(comparator_2_gt));  // open: eq, lt
  Comparator #(.mode("unsigned"), .width(4)) comparator_3 (
    .a(Proximity), .b(4'b0010), .gt(comparator_3_gt));  // open: eq, lt
  not not_3 (not_3_out, ZoneDIsplay[1]);
  not not_4 (not_4_out, comparator_2_gt);
  Comparator #(.mode("unsigned"), .width(4)) comparator_4 (
    .a(Speed), .b(4'b0110), .gt(comparator_4_gt));  // open: eq, lt
  Comparator #(.mode("unsigned"), .width(4)) comparator_5 (
    .a(Speed), .b(4'b1001), .gt(comparator_5_gt));  // open: eq, lt
  and and_1 (and_1_out, not_1_out, not_2_out);
  and and_2 (and_2_out, comparator_3_gt, not_3_out);
  not not_5 (not_5_out, comparator_5_gt);
  or or_1 (ZoneDIsplay[0], comparator_2_gt, and_2_out);
  CorridorCounters corridorcounters_1 (
    .CorridorSelect(in_5), .CrossingPulse(in_6), .in_3(CLK), .RESET(Reset), .Counter_C1(out_14),
    .Counter_C2(out_15), .Counter_C3(out_16), .Counter_C4(out_17));
  not not_6 (not_6_out, comparator_4_gt);
  LED led_1 (.in(not_6_out));
  and and_3 (and_3_out, comparator_4_gt, not_5_out);
  LED led_2 (.in(and_3_out));
  LED led_3 (.in(comparator_5_gt));
  and and_4 (BUZZER_ALARM, and_1_out, not_3_out);
  not not_7 (LED_GREEN, or_2_out);
  and and_5 (LED_YELLOW, or_3_out, not_8_out);
  or or_2 (or_2_out, not_8_out, LED_YELLOW);
  and and_6 (and_6_out, and_1_out, TimeOfDay);
  not not_8 (not_8_out, BUZZER_ALARM);
  or or_3 (or_3_out, not_4_out, and_6_out);

  assign LED_RED = BUZZER_ALARM;

  // Notes on the sheet:
  //   CorridorSelect
  //   CrossingPulse
  //   NIGHT
  //   NOT_D1
  //   NOT_D0
  //   P_GT_4
  //   P_GT_8
  //   P_GT_2
  //   TOWARD
  //   NORMAL
  //   RAPID
  //   HIGH
  //   COUNTER_C1
  //   COUNTER_C2
  //   COUNTER_C3
  //   COUNTER_C4
endmodule

module CorridorCounters (
  input  [1:0] CorridorSelect,
  input  CrossingPulse,
  input  in_3,
  input  RESET,
  output [7:0] Counter_C1,
  output [7:0] Counter_C2,
  output [7:0] Counter_C3,
  output [7:0] Counter_C4
);

  wire and_1_out, and_2_out, and_3_out, and_4_out, not_1_out, not_2_out;

  not not_1 (not_1_out, CorridorSelect[0]);
  not not_2 (not_2_out, CorridorSelect[1]);
  and and_1 (and_1_out, not_1_out, not_2_out, CrossingPulse);
  and and_2 (and_2_out, not_2_out, CorridorSelect[0], CrossingPulse);
  and and_3 (and_3_out, CorridorSelect[1], CorridorSelect[0], CrossingPulse);
  // Probe on and_1_out
  // Probe on and_2_out
  and and_4 (and_4_out, CorridorSelect[1], not_1_out, CrossingPulse);
  // Probe on and_4_out
  // Probe on and_3_out
  Counter #(.ongoal("stay")) C1 (
    .clr(RESET), .load(1'b0), .up(1'b1), .count(and_1_out), .clk(in_3), .Q(Counter_C1));  // open: D, carry
  Counter C3 (.clr(RESET), .load(1'b0), .up(1'b1), .count(and_4_out), .clk(in_3), .Q(Counter_C3));  // open: D, carry
  Counter C2 (.clr(RESET), .load(1'b0), .up(1'b1), .count(and_2_out), .clk(in_3), .Q(Counter_C2));  // open: D, carry
  Counter C4 (.clr(RESET), .load(1'b0), .up(1'b1), .count(and_3_out), .clk(in_3), .Q(Counter_C4));  // open: D, carry

  // Notes on the sheet:
  //   CLK
  //   NOT_C0
  //   NOT_C1
  //   E1
  //   E2
  //   E3
  //   E4
endmodule
